// Logisim project Projetocircuit.circ as structural Verilog
module main (
  input  [3:0] in_1,
  input  [3:0] in_2,
  output [3:0] out_3
);

  wire add1_1_p4, add1_1_p5, add1_3_vai_1, add1_4_vai_1;

  // Probe on in_2
  // Add1 add1_1: pin names not known; wires that end beside it: in_2[3], out_3[3], in_1[3], add1_1_p4, add1_1_p5, add1_1_p4
  Add1 add1_2 (.A(add1_3_vai_1), .B(in_1[2]), .Vem_1(in_2[2]), .Soma(out_3[2]), .Vai_1(add1_1_p5));
  Add1 add1_3 (.A(add1_4_vai_1), .B(in_1[1]), .Vem_1(in_2[1]), .Soma(out_3[1]), .Vai_1(add1_3_vai_1));
  // Probe on out_3
  Add1 add1_4 (.A(1'b0), .B(in_1[0]), .Vem_1(in_2[0]), .Soma(out_3[0]), .Vai_1(add1_4_vai_1));
  // Probe on in_1
endmodule

module Add1 (
  input  A,
  input  B,
  input  Vem_1,
  output Soma,
  output Vai_1
);

  wire B___C__x_A_out, B___C_out, B_x_C_out, xor_1_out;

  xor xor_1 (xor_1_out, A, B);
  or B___C (B___C_out, B, Vem_1);
  xor xor_2 (Soma, xor_1_out, Vem_1);
  and B___C__x_A (B___C__x_A_out, B___C_out, A);
  and B_x_C (B_x_C_out, B, Vem_1);
  or A_B___C____B_x_C (Vai_1, B___C__x_A_out, B_x_C_out);
endmodule
